// Logisim project 18BCE247.circ as structural Verilog: 4 circuits, main circuit main
module main (
  input  [3:0] A,
  input  [3:0] B,
  input  [1:0] S0_prime_S1_prime,
  input  S0,
  input  [1:0] S1S2,
  output out_6,
  output [3:0] Output
);

  wire [3:0] arithmetic_unit_1_output, logical_unit_1_output, shift_unit_1_output;

  Arithmetic_Unit arithmetic_unit_1 (.A(A), .B(B), .S1S0(S1S2), .Output(arithmetic_unit_1_output), .out_5(out_6));
  Logical_Unit logical_unit_1 (.A(A), .B(B), .in_3(S1S2), .Output(logical_unit_1_output));
  Shift_Unit shift_unit_1 (.A(A), .S0(S0), .Output(shift_unit_1_output));
  Multiplexer #(.select(2), .width(4)) multiplexer_1 (
    .in0(arithmetic_unit_1_output), .in1(logical_unit_1_output), .in2(shift_unit_1_output), .out(Output),
    .sel(S0_prime_S1_prime));  // open: in3, en

  // Notes on the sheet:
  //   4 - Bit Arithmetic Logical and Shift Unit (ALS Unit)
  //   Submitted By : 
  //   Urvashi Ramdasani
  //   18BCE247 D Division
endmodule

// AU
module Arithmetic_Unit (
  input  [3:0] A,
  input  [3:0] B,
  input  [1:0] S1S0,
  output [3:0] Output,
  output out_5
);

  wire adder_1_cout, adder_2_cout, adder_3_cout, multiplexer_1_out, multiplexer_2_out, multiplexer_3_out,
       multiplexer_4_out, not_1_out, not_2_out, not_3_out, not_4_out, not_5_out, not_6_out, not_7_out,
       not_8_out, xor_1_out;

  not not_1 (not_1_out, B[0]);
  not not_2 (not_2_out, 1'b0);
  not not_3 (not_3_out, B[1]);
  not not_4 (not_4_out, 1'b0);
  not not_5 (not_5_out, B[2]);
  not not_6 (not_6_out, 1'b0);
  not not_7 (not_7_out, B[3]);
  not not_8 (not_8_out, 1'b0);
  Multiplexer #(.select(2)) multiplexer_1 (
    .in0(B[0]), .in1(not_1_out), .in2(1'b0), .in3(not_2_out), .out(multiplexer_1_out), .sel(S1S0));  // open: en
  Multiplexer #(.select(2)) multiplexer_2 (
    .in0(B[1]), .in1(not_3_out), .in2(1'b0), .in3(not_4_out), .out(multiplexer_2_out), .sel(S1S0));  // open: en
  Multiplexer #(.select(2)) multiplexer_3 (
    .in0(B[2]), .in1(not_5_out), .in2(1'b0), .in3(not_6_out), .out(multiplexer_3_out), .sel(S1S0));  // open: en
  Multiplexer #(.select(2)) multiplexer_4 (
    .in0(B[3]), .in1(not_7_out), .in2(1'b0), .in3(not_8_out), .out(multiplexer_4_out), .sel(S1S0));  // open: en
  xor xor_1 (xor_1_out, S1S0[1], S1S0[0]);
  Adder #(.width(1)) adder_1 (.a(A[0]), .b(multiplexer_1_out), .out(Output[0]), .cin(xor_1_out), .cout(adder_1_cout));
  Adder #(.width(1)) adder_2 (
    .a(A[1]), .b(multiplexer_2_out), .out(Output[1]), .cin(adder_1_cout), .cout(adder_2_cout));
  Adder #(.width(1)) adder_3 (
    .a(A[2]), .b(multiplexer_3_out), .out(Output[2]), .cin(adder_2_cout), .cout(adder_3_cout));
  Adder #(.width(1)) adder_4 (.a(A[3]), .b(multiplexer_4_out), .out(Output[3]), .cin(adder_3_cout), .cout(out_5));

  // Notes on the sheet:
  //   4 - bit Arithmetic Circuit
endmodule

// LU
module Logical_Unit (
  input  [3:0] A,
  input  [3:0] B,
  input  [1:0] in_3,
  output [3:0] Output
);

  wire [3:0] and_1_out, not_1_out, or_1_out, xor_1_out;

  assign and_1_out = A & B;  // AND_Gate and_1, 4 bits wide
  assign or_1_out = A | B;  // OR_Gate or_1, 4 bits wide
  assign xor_1_out = A ^ B;  // XOR_Gate xor_1, 4 bits wide
  assign not_1_out = ~A;  // NOT_Gate not_1, 4 bits wide
  Multiplexer #(.select(2), .width(4)) multiplexer_1 (
    .in0(and_1_out), .in1(or_1_out), .in2(xor_1_out), .in3(not_1_out), .out(Output), .sel(in_3));  // open: en

  // Notes on the sheet:
  //   4 - bit Logical Unit
endmodule

// ShU
module Shift_Unit (
  input  [3:0] A,
  input  S0,
  output [3:0] Output
);

  Multiplexer multiplexer_1 (.in0(A[3]), .in1(A[1]), .out(Output[0]), .sel(S0));  // open: en
  Multiplexer multiplexer_2 (.in0(A[0]), .in1(A[2]), .out(Output[1]), .sel(S0));  // open: en
  Multiplexer multiplexer_3 (.in0(A[1]), .in1(A[3]), .out(Output[2]), .sel(S0));  // open: en
  Multiplexer multiplexer_4 (.in0(A[2]), .in1(A[0]), .out(Output[3]), .sel(S0));  // open: en

  // Notes on the sheet:
  //   4 - Bit Shift Unit
  //   S0 = 
  //   S0 = 
  //   0 - Circular Shift Left
  //   1 - Circular Shift Right
endmodule
