// Logisim project 18BCE247_assignment2.circ as structural Verilog: 4 circuits, main circuit Main Associative Memory
module Main_Associative_Memory (
  input  [7:0] Argument,
  input  [7:0] Key,
  input  [7:0] Input,
  input  Write,
  input  Read,
  input  [2:0] Address,
  output [7:0] Match,
  output [7:0] Output
);

  wire _1st, _2nd, _3rd, _4th, _5th, _6th, _7th, _8th, and_1_out, and_2_out, and_3_out, and_4_out, and_5_out,
       and_6_out, and_7_out, and_8_out, Clock_out, decoder_1_out0, decoder_1_out1, decoder_1_out2,
       decoder_1_out3, decoder_1_out4, decoder_1_out5, decoder_1_out6, decoder_1_out7;
  wire [2:0] counter_1_q;
  wire [7:0] _1, _2, _3, _4, _5, _6, _7, _8;

  Clock Clock (.out(Clock_out));
  and and_1 (and_1_out, Read, Match[4]);
  and and_2 (and_2_out, Match[0], Read);
  Single_Word Word_1 (
    .Input(Input), .Write(_1st), .Read(and_2_out), .Clock(Clock_out), .Output(_1), .M(Match[0]), .K(Key),
    .A(Argument));
  and and_3 (and_3_out, Read, Match[5]);
  Single_Word Word_5 (
    .Input(Input), .Write(_5th), .Read(and_1_out), .Clock(Clock_out), .Output(_5), .M(Match[4]), .K(Key),
    .A(Argument));
  and and_4 (and_4_out, Match[1], Read);
  Single_Word Word_2 (
    .Input(Input), .Write(_2nd), .Read(and_4_out), .Clock(Clock_out), .Output(_2), .M(Match[1]), .K(Key),
    .A(Argument));
  and and_5 (and_5_out, Match[2], Read);
  and and_6 (and_6_out, Read, Match[6]);
  Single_Word Word_6 (
    .Input(Input), .Write(_6th), .Read(and_3_out), .Clock(Clock_out), .Output(_6), .M(Match[5]), .K(Key),
    .A(Argument));
  Single_Word Word_3 (
    .Input(Input), .Write(_3rd), .Read(and_5_out), .Clock(Clock_out), .Output(_3), .M(Match[2]), .K(Key),
    .A(Argument));
  Single_Word Word_7 (
    .Input(Input), .Write(_7th), .Read(and_6_out), .Clock(Clock_out), .Output(_7), .M(Match[6]), .K(Key),
    .A(Argument));
  and and_7 (and_7_out, Match[3], Read);
  and and_8 (and_8_out, Read, Match[7]);
  Single_Word Word_4 (
    .Input(Input), .Write(_4th), .Read(and_7_out), .Clock(Clock_out), .Output(_4), .M(Match[3]), .K(Key),
    .A(Argument));
  Single_Word Word_8 (
    .Input(Input), .Write(_8th), .Read(and_8_out), .Clock(Clock_out), .Output(_8), .M(Match[7]), .K(Key),
    .A(Argument));
  Multiplexer #(.select(3), .width(8)) multiplexer_1 (
    .in0(_1), .in1(_2), .in2(_3), .in3(_4), .in4(_5), .in5(_6), .in6(_7), .in7(_8), .out(Output),
    .sel(counter_1_q));  // open: en
  Counter #(.width(3), .max('h7)) counter_1 (.Q(counter_1_q), .clk(Clock_out));  // open: load, D, count, carry, clr
  and and_9 (_1st, decoder_1_out0, Write);
  and and_10 (_2nd, decoder_1_out1, Write);
  and and_11 (_3rd, decoder_1_out2, Write);
  and and_12 (_4th, decoder_1_out3, Write);
  and and_13 (_5th, decoder_1_out4, Write);
  and and_14 (_6th, decoder_1_out5, Write);
  and and_15 (_7th, decoder_1_out6, Write);
  and and_16 (_8th, decoder_1_out7, Write);
  Decoder #(.select(3)) decoder_1 (
    .out0(decoder_1_out0), .out1(decoder_1_out1), .out2(decoder_1_out2), .out3(decoder_1_out3),
    .out4(decoder_1_out4), .out5(decoder_1_out5), .out6(decoder_1_out6), .out7(decoder_1_out7), .sel(Address));  // open: en

  // Other names for the same wires on the sheet: A[7:0] = Argument; K[7:0] = Key; M1 = Match[0]; M2 = Match[1];
  //   M3 = Match[2]; M4 = Match[3]; M5 = Match[4]; M6 = Match[5]; M7 = Match[6]; M8 = Match[7]

  // Notes on the sheet:
  //   Submitted By : 
  //   Urvashi Ramdasani
  //   18BCE247 D Division
endmodule

module Single_Word (
  input  [7:0] Input,
  input  Write,
  input  Read,
  input  Clock,
  input  [7:0] A,
  input  [7:0] K,
  output [7:0] Output,
  output M
);

  wire _0_m, _1_m, _2_m, _3_m, _4_m, _5_m, _6_m, _7_m;

  Single_Cell _7 (
    .Input(Input[7]), .Write(Write), .Read(Read), .M(_7_m), .Output(Output[7]), .A(A[7]), .K(K[7]),
    .Clock(Clock));
  Single_Cell _6 (
    .Input(Input[6]), .Write(Write), .Read(Read), .M(_6_m), .Output(Output[6]), .A(A[6]), .K(K[6]),
    .Clock(Clock));
  Single_Cell _5 (
    .Input(Input[5]), .Write(Write), .Read(Read), .M(_5_m), .Output(Output[5]), .A(A[5]), .K(K[5]),
    .Clock(Clock));
  and and_1 (M, _7_m, _6_m, _5_m, _4_m, _3_m, _2_m, _1_m, _0_m);
  Single_Cell _4 (
    .Input(Input[4]), .Write(Write), .Read(Read), .M(_4_m), .Output(Output[4]), .A(A[4]), .K(K[4]),
    .Clock(Clock));
  Single_Cell _3 (
    .Input(Input[3]), .Write(Write), .Read(Read), .M(_3_m), .Output(Output[3]), .A(A[3]), .K(K[3]),
    .Clock(Clock));
  Single_Cell _2 (
    .Input(Input[2]), .Write(Write), .Read(Read), .M(_2_m), .Output(Output[2]), .A(A[2]), .K(K[2]),
    .Clock(Clock));
  Single_Cell _1 (
    .Input(Input[1]), .Write(Write), .Read(Read), .M(_1_m), .Output(Output[1]), .A(A[1]), .K(K[1]),
    .Clock(Clock));
  Single_Cell _0 (
    .Input(Input[0]), .Write(Write), .Read(Read), .M(_0_m), .Output(Output[0]), .A(A[0]), .K(K[0]),
    .Clock(Clock));
endmodule

module Single_Cell (
  input  A,
  input  K,
  input  Input,
  input  Write,
  input  Read,
  input  Clock,
  output M,
  output Output
);

  wire and_1_out, and_2_out, not_1_out, s_r_ff_1_q;

  not not_1 (not_1_out, Input);
  and and_1 (and_1_out, Input, Write);
  and and_2 (and_2_out, not_1_out, Write);
  S_R_Flip_Flop s_r_ff_1 (.S(and_1_out), .clk(Clock), .R(and_2_out), .Q(s_r_ff_1_q));  // open: Qn, preset, reset, en
  Match_Logic match_logic_1 (.F(s_r_ff_1_q), .A(A), .K(K), .M(M));
  and and_3 (Output, s_r_ff_1_q, Read);
endmodule

// M. L
module Match_Logic (
  input  A,
  input  F,
  input  K,
  output M
);

  wire not_1_out, xnor_1_out;

  xnor xnor_1 (xnor_1_out, F, A);
  not not_1 (not_1_out, K);
  or or_1 (M, xnor_1_out, not_1_out);
endmodule
