// Logisim project 6B Division 4bits.circ as structural Verilog: 3 circuits, main circuit Division
// E LOAD
module Division (
  input  [7:0] Dividend,
  input  [3:0] Divisor
);

  wire A_LOAD, ADD_SUB, B_LOAD, B_Sign_q, button_1_out, E, E_LOAD, E_out, Q_LOAD, Q_Sign_q, SC_DEC, SC_LOAD,
       SHL_EAQ, xor_1_out;
  wire [2:0] SC;
  wire [3:0] A, A_out, B, multiplexer_1_out, multiplexer_2_out, Q, Q_out;

  Button button_1 (.out(button_1_out));
  Multiplexer #(.width(4), .enable("false")) multiplexer_1 (
    .in0(A_out), .in1(Dividend[7:4]), .out(multiplexer_1_out), .sel(B_LOAD));
  Multiplexer #(.width(4), .enable("false")) multiplexer_2 (
    .in0(Q_out), .in1(Dividend[3:0]), .out(multiplexer_2_out), .sel(B_LOAD));
  Register #(.width(4)) u_B (.D(Divisor), .en(B_LOAD), .Q(B), .clk(button_1_out));  // open: clr
  Register #(.width(1)) u_E (.D(E_out), .en(E_LOAD), .Q(E), .clk(button_1_out), .clr(B_LOAD));
  Register #(.width(4)) u_A (.D(multiplexer_1_out), .en(A_LOAD), .Q(A), .clk(button_1_out));  // open: clr
  ALS_Unit als_unit_1 (
    .SHL(SHL_EAQ), .B(B), .ADD_SUB(ADD_SUB), .A_out(A_out), .E_out(E_out), .E(E), .A(A), .Q(Q), .Q_out(Q_out));
  D_Flip_Flop A_Sign (.clk(button_1_out), .en(B_LOAD));  // open: D, Q, Qn, preset, reset
  D_Flip_Flop B_Sign (.clk(button_1_out), .Q(B_Sign_q), .en(B_LOAD));  // open: D, Qn, preset, reset
  Register #(.width(4)) u_Q (.D(multiplexer_2_out), .en(Q_LOAD), .Q(Q), .clk(button_1_out));  // open: clr
  xor xor_1 (xor_1_out, B_Sign_q, Q_Sign_q);
  D_Flip_Flop Q_Sign (.clk(button_1_out), .D(xor_1_out), .Q(Q_Sign_q), .en(B_LOAD));  // open: Qn, preset, reset
  Counter #(.width(3), .max('h4)) u_SC (
    .load(SC_LOAD), .D(3'b100), .count(SC_DEC), .Q(SC), .clk(button_1_out));  // open: carry, clr
  Control_Unit control_unit_1 (
    .E(E), .SC(SC), .Clock(button_1_out), .SHL_ALS(SHL_EAQ), .A_load(A_LOAD), .B_load(B_LOAD),
    .SC_load(SC_LOAD), .SC_Decrement(SC_DEC), .Q_load(Q_LOAD), .E_load(E_LOAD), .ADD_SUB(ADD_SUB));
endmodule

// ALS
module ALS_Unit (
  input  E,
  input  [3:0] A,
  input  [3:0] Q,
  input  SHL,
  input  [3:0] B,
  input  ADD_SUB,
  output [3:0] Q_out,
  output [3:0] A_out,
  output E_out
);

  wire adder_1_cout, not_2_out;
  wire [3:0] adder_1_out, multiplexer_1_out, not_1_out;
  wire [8:0] shifter_1_out;

  Multiplexer #(.width(4), .enable("false")) multiplexer_1 (
    .in0(B), .in1(not_1_out), .out(multiplexer_1_out), .sel(ADD_SUB));
  assign not_1_out = ~B;  // NOT_Gate not_1, 4 bits wide
  Shifter #(.width(9)) shifter_1 (.in({E, A, Q}), .\dist (4'b0001), .out(shifter_1_out));
  not not_2 (not_2_out, SHL);
  Adder #(.width(4)) adder_1 (.a(A), .b(multiplexer_1_out), .out(adder_1_out), .cin(ADD_SUB), .cout(adder_1_cout));
  Multiplexer #(.width(4), .enable("false")) multiplexer_2 (
    .in0(shifter_1_out[3:0]), .in1({Q[3:1], 1'b1}), .out(Q_out), .sel(not_2_out));
  Multiplexer #(.width(4), .enable("false")) multiplexer_3 (
    .in0(shifter_1_out[7:4]), .in1(adder_1_out), .out(A_out), .sel(not_2_out));
  Multiplexer #(.enable("false")) multiplexer_4 (
    .in0(shifter_1_out[8]), .in1(adder_1_cout), .out(E_out), .sel(not_2_out));
endmodule

// Control
module Control_Unit (
  input  E,
  input  [2:0] SC,
  input  Clock,
  output ADD_SUB,
  output SHL_ALS,
  output A_load,
  output B_load,
  output SC_load,
  output SC_Decrement,
  output Q_load,
  output E_load
);

  wire and_1_out, and_2_out, and_3_out, and_4_out, decoder_1_out4, not_1_out, not_2_out, not_3_out,
       not_4_out, or_1_out;
  wire [2:0] multiplexer_1_out, Timing_q;

  Multiplexer #(.width(3), .enable("false")) multiplexer_1 (
    .in0(3'b000), .in1(3'b001), .out(multiplexer_1_out), .sel(or_1_out));
  or or_1 (or_1_out, SC[0], SC[1], SC[2]);
  Decoder #(.select(3), .enable("false")) decoder_1 (
    .out0(B_load), .out1(SHL_ALS), .out2(ADD_SUB), .out3(SC_Decrement), .out4(decoder_1_out4), .sel(Timing_q));  // open: out5, out6, out7
  Counter #(.width(3), .max('h4)) Timing (
    .load(decoder_1_out4), .D(multiplexer_1_out), .count(not_1_out), .Q(Timing_q), .clk(Clock));  // open: carry, clr
  not not_1 (not_1_out, decoder_1_out4);
  not not_2 (not_2_out, E);
  not not_3 (not_3_out, E);
  not not_4 (not_4_out, E);
  and and_1 (and_1_out, SC_Decrement, not_2_out);
  and and_2 (and_2_out, SC_Decrement, E);
  and and_3 (and_3_out, ADD_SUB, not_3_out);
  and and_4 (and_4_out, SC_Decrement, not_4_out);
  or or_2 (A_load, B_load, SHL_ALS, ADD_SUB, and_1_out);
  or or_3 (SC_load, B_load, SC_Decrement);
  or or_4 (Q_load, B_load, SHL_ALS, and_2_out);
  or or_5 (E_load, and_3_out, and_4_out, SHL_ALS);

  // Other names for the same wires on the sheet: T0 = B_load; T1 = SHL_ALS; T2 = ADD_SUB; T3 = SC_Decrement
endmodule
