// Logisim project binary_exess3.circ as structural Verilog: 1 circuit, main circuit main
module main (
  input  [3:0] in_1,
  input  [3:0] in_2,
  input  [3:0] in_3,
  output out_4,
  output [3:0] out_5
);

  wire adder_1_cout, and_1_out, or_1_out;
  wire [3:0] adder_1_out;

  Adder #(.width(4)) adder_1 (.a(in_1), .b(in_2), .out(adder_1_out), .cout(adder_1_cout));  // open: cin
  or or_1 (or_1_out, adder_1_out[2], adder_1_out[3]);
  and and_1 (and_1_out, adder_1_out[0], adder_1_out[1], or_1_out);
  Adder #(.width(4)) adder_2 (.a(in_3), .b(adder_1_out), .out(out_5));  // open: cin, cout
  or or_2 (out_4, and_1_out, adder_1_cout);

  // Notes on the sheet:
  //   Binary to Exess-3
endmodule
