// Logisim project p3.circ as structural Verilog: 1 circuit, main circuit main
module main (
  input  A,
  input  A_2,
  input  B,
  input  B_2,
  input  C,
  input  A_3,
  input  B_3,
  input  A_4,
  input  C_2,
  input  B_4
);

  wire and_1_out, and_2_out, and_3_out, and_4_out, AND_5_out, AND_6_out, AND_7_out, not_1_out, not_2_out,
       or_1_out, or_2_out, OR_3_out, xor_1_out, xor_2_out, xor_3_out, xor_4_out, xor_5_out, xor_6_out;

  xor xor_1 (xor_1_out, A_2, B_2);
  and and_1 (and_1_out, A_2, B_2);
  xor xor_2 (xor_2_out, A_4, B_4);
  and and_2 (and_2_out, A_4, B_4);
  LED led_1 (.in(xor_2_out));
  LED led_2 (.in(and_2_out));
  xor xor_3 (xor_3_out, xor_1_out, C);
  and and_3 (and_3_out, xor_1_out, C);
  LED led_3 (.in(xor_3_out));
  or or_1 (or_1_out, and_3_out, and_1_out);
  LED led_4 (.in(or_1_out));
  xor xor_4 (xor_4_out, A, B);
  not not_1 (not_1_out, A);
  xor xor_5 (xor_5_out, A_3, B_3);
  not not_2 (not_2_out, A_3);
  and and_4 (and_4_out, not_1_out, B);
  and AND_5 (AND_5_out, not_2_out, B_3);
  and AND_6 (AND_6_out, B_3, C_2);
  and AND_7 (AND_7_out, not_2_out, C_2);
  LED led_5 (.in(xor_4_out));
  LED led_6 (.in(and_4_out));
  xor xor_6 (xor_6_out, xor_5_out, C_2);
  or or_2 (or_2_out, AND_5_out, AND_6_out);
  LED led_7 (.in(xor_6_out));
  LED led_8 (.in(OR_3_out));
  or OR_3 (OR_3_out, or_2_out, AND_7_out);

  // Notes on the sheet:
  //   XOR
  //   AND
  //   Full Adder
  //   XOR
  //   AND
  //   Half Adder
  //   XOR
  //   AND
  //   S
  //   C
  //   OR
  //   S
  //   C
  //   Full Subtractor
  //   NOT
  //   XOR
  //   NOT
  //   Half Subtractor
  //   XOR
  //   AND
  //   D
  //   B
  //   XOR
  //   OR
  //   D
  //   B
endmodule
