// Logisim project prac6.circ as structural Verilog: 1 circuit, main circuit main
module main (
  input  [1:0] C,
  input  B,
  input  A,
  input  [1:0] in_4
);

  wire multiplexer_1_out, multiplexer_2_out, not_1_out, or_1_out;

  not not_1 (not_1_out, A);
  Multiplexer #(.select(2)) multiplexer_1 (
    .in0(1'b0), .in1(1'b1), .in2(B), .in3(B), .out(multiplexer_1_out), .sel(C), .en(not_1_out));
  Multiplexer #(.select(2)) multiplexer_2 (
    .in0(B), .in1(1'b0), .in2(B), .in3(B), .out(multiplexer_2_out), .sel(in_4), .en(A));
  or or_1 (or_1_out, multiplexer_1_out, multiplexer_2_out);
  LED led_1 (.in(or_1_out));

  // Notes on the sheet:
  //   I1 = 1
  //   GND
  //   GND
  //   D
  //   C
  //   D
  //   OR
endmodule
