// Logisim project prac6a.circ as structural Verilog: 1 circuit, main circuit main
module main (
  input  in_1,
  input  [2:0] in_2
);

  wire multiplexer_1_out, not_1_out;

  not not_1 (not_1_out, in_1);
  Multiplexer #(.select(3)) multiplexer_1 (
    .in0(1'b0), .in1(not_1_out), .in2(1'b0), .in3(1'b0), .in4(in_1), .in5(not_1_out), .in6(1'b1), .in7(1'b1),
    .out(multiplexer_1_out), .sel(in_2));  // open: en
  LED led_1 (.in(multiplexer_1_out));
endmodule
