// Logisim project prac7.circ as structural Verilog: 1 circuit, main circuit main
module main (
  input  R,
  input  D,
  input  S,
  input  K,
  input  T,
  input  J
);

  wire and_1_out, and_2_out, and_3_out, and_4_out, clock_1_out, clock_2_out, clock_3_out, nand_1_out,
       nand_2_out, nand_3_out, nand_4_out, nand_5_out, nand_6_out, nand_7_out, nand_8_out, nor_1_out,
       nor_2_out, not_1_out;

  Clock clock_1 (.out(clock_1_out));
  nor nor_1 (nor_1_out, R, nor_2_out);
  nor nor_2 (nor_2_out, nor_1_out, S);
  and and_1 (and_1_out, nand_1_out, K, clock_1_out);
  and and_2 (and_2_out, clock_1_out, J, nand_2_out);
  LED led_1 (.in(nor_1_out));
  LED led_2 (.in(nor_2_out));
  nand nand_1 (nand_1_out, and_1_out, nand_2_out);
  nand nand_2 (nand_2_out, nand_1_out, and_2_out);
  Clock clock_2 (.out(clock_2_out));
  LED led_3 (.in(nand_1_out));
  LED led_4 (.in(nand_2_out));
  not not_1 (not_1_out, D);
  nand nand_3 (nand_3_out, D, clock_2_out);
  nand nand_4 (nand_4_out, clock_2_out, not_1_out);
  Clock clock_3 (.out(clock_3_out));
  and and_3 (and_3_out, nand_7_out, T, clock_3_out);
  and and_4 (and_4_out, clock_3_out, T, nand_8_out);
  LED led_5 (.in(nand_5_out));
  nand nand_5 (nand_5_out, nand_3_out, nand_6_out);
  nand nand_6 (nand_6_out, nand_5_out, nand_4_out);
  LED led_6 (.in(nand_6_out));
  nand nand_7 (nand_7_out, and_3_out, nand_8_out);
  nand nand_8 (nand_8_out, nand_7_out, and_4_out);
  LED led_7 (.in(nand_7_out));
  LED led_8 (.in(nand_8_out));

  // Notes on the sheet:
  //   R-S Flip Flop
  //   Q
  //   Q'
  //   J-K Flip Flop
  //   Q
  //   Q'
  //   D Flip Flop
  //   T Flip Flop
  //   Q
  //   Q'
  //   Q
  //   Q'
endmodule
