// Logisim project prac8.circ as structural Verilog: 1 circuit, main circuit main
module main (
);

  wire and_1_out, and_2_out, clock_1_out, j_k_ff_1_q, j_k_ff_1_qn, j_k_ff_2_q, j_k_ff_2_qn, j_k_ff_3_q,
       j_k_ff_3_qn, j_k_ff_4_q, j_k_ff_4_qn;

  Clock clock_1 (.out(clock_1_out));
  J_K_Flip_Flop j_k_ff_1 (
    .J(1'b1), .clk(clock_1_out), .K(1'b1), .Q(j_k_ff_1_q), .Qn(j_k_ff_1_qn));  // open: preset, en, reset
  J_K_Flip_Flop j_k_ff_2 (
    .J(j_k_ff_1_q), .clk(clock_1_out), .K(j_k_ff_1_q), .Q(j_k_ff_2_q), .Qn(j_k_ff_2_qn));  // open: preset, en, reset
  and and_1 (and_1_out, j_k_ff_1_q, j_k_ff_2_q);
  LED led_1 (.in(j_k_ff_4_qn));
  LED led_2 (.in(j_k_ff_4_q));
  J_K_Flip_Flop j_k_ff_3 (
    .J(and_1_out), .clk(clock_1_out), .K(and_1_out), .Q(j_k_ff_3_q), .Qn(j_k_ff_3_qn));  // open: preset, en, reset
  LED led_3 (.in(j_k_ff_2_qn));
  LED led_4 (.in(j_k_ff_3_qn));
  LED led_5 (.in(j_k_ff_2_q));
  LED led_6 (.in(j_k_ff_3_q));
  and and_2 (and_2_out, and_1_out, j_k_ff_3_q);
  LED led_7 (.in(j_k_ff_1_qn));
  LED led_8 (.in(j_k_ff_1_q));
  J_K_Flip_Flop j_k_ff_4 (
    .J(and_2_out), .clk(clock_1_out), .K(and_2_out), .Q(j_k_ff_4_q), .Qn(j_k_ff_4_qn));  // open: preset, en, reset

  // Notes on the sheet:
  //   Synchronus Up and Down Counter
endmodule
