// Logisim project prac9.circ as structural Verilog: 1 circuit, main circuit main
module main (
);

  wire clock_1_out, t_ff_1_q, t_ff_1_qn, t_ff_2_q, t_ff_2_qn, t_ff_3_qn;

  Clock clock_1 (.out(clock_1_out));
  T_Flip_Flop t_ff_1 (.clk(clock_1_out), .T(1'b1), .Q(t_ff_1_q), .Qn(t_ff_1_qn));  // open: preset, reset, en
  T_Flip_Flop t_ff_2 (.clk(t_ff_1_q), .T(1'b1), .Q(t_ff_2_q), .Qn(t_ff_2_qn));  // open: preset, reset, en
  T_Flip_Flop t_ff_3 (.clk(t_ff_2_q), .T(1'b1), .Qn(t_ff_3_qn));  // open: Q, preset, reset, en
  LED led_1 (.in(t_ff_3_qn));
  LED led_2 (.in(t_ff_2_qn));
  LED led_3 (.in(t_ff_1_qn));

  // Notes on the sheet:
  //   Ripple Counter
endmodule
